// Logisim project gigatron.circ as structural Verilog: 1 circuit, main circuit main
module main (
  input  in_1,
  input  in_2,
  input  in_3,
  input  in_4,
  input  in_5,
  input  in_6,
  input  in_7,
  input  in_8,
  input  in_9,
  input  in_10,
  input  in_11,
  input  in_12,
  input  in_13,
  input  in_14,
  input  in_15,
  input  in_16,
  input  in_17,
  input  in_18,
  input  in_19,
  input  in_20,
  input  in_21,
  input  in_22,
  input  in_23,
  input  in_24,
  input  in_25,
  input  in_26,
  input  in_27,
  input  in_28,
  input  in_29,
  input  in_30,
  input  in_31,
  input  in_32,
  input  in_33,
  input  in_34,
  input  in_35,
  input  in_36,
  input  in_37,
  input  in_38,
  input  in_39,
  input  in_40,
  input  in_41,
  input  in_42,
  input  in_43,
  input  in_44,
  input  in_45,
  input  in_46,
  input  in_47,
  input  in_48,
  input  in_49,
  input  in_50,
  input  in_51,
  input  in_52,
  input  in_53,
  input  in_54,
  input  in_55
);

  wire AC0, AC1, AC2, AC3, AC4, AC5, AC6, AC7, AE, AL, ALU0, ALU1, ALU2, ALU3, ALU4, ALU5, ALU6, ALU7,
       and_2_out, AR0, AR1, AR2, AR3, BUS0, BUS1, BUS2, BUS3, BUS4, BUS5, BUS6, BUS7, button_1_out, CLK1,
       CLK2, CO, D0, D1, D2, D3, D4, D5, D6, D7, DE, EH, EL, IE, IR0, IR1, IR2, IR3, IR4, IR5, IR6, IR7, IX,
       LD, n7404_1_pin12, n74138_1_pin7, n74138_1_pin9, n74138_1_pin10, n74138_1_pin11, n74138_1_pin12,
       n74138_1_pin13, n74138_1_pin14, n74138_1_pin15, n74138_2_pin7, n74138_2_pin9, n74138_2_pin12,
       n74138_2_pin13, n74138_2_pin14, n74138_2_pin15, n74139_2_pin4, n74153_1_pin7, n74153_2_pin7,
       n74153_2_pin9, n74153_3_pin7, n74153_3_pin9, n74153_4_pin7, n74153_4_pin9, n74153_5_pin7,
       n74153_5_pin9, n74153_6_pin7, n74153_6_pin9, n74153_7_pin7, n74153_7_pin9, n74153_8_pin7,
       n74153_8_pin9, n74153_9_pin7, n74153_9_pin9, n74161_1_pin15, n74161_2_pin15, n74161_3_pin15,
       n74161_4_pin15, n74161_5_pin15, n74161_6_pin15, n74161_9_pin10, n74240_1_pin7, n74240_1_pin9,
       n74240_1_pin12, n74283_1_pin9, not_2_out, not_3_out, not_4_out, not_5_out, not_6_out, not_8_out, OE,
       OL, or_2_out, or_3_out, or_4_out, or_5_out, or_6_out, or_7_out, or_8_out, OUT0, OUT1, OUT2, OUT3,
       OUT4, OUT5, OUT6, OUT7, PC0, PC1, PC2, PC3, PC4, PC5, PC6, PC7, PC8, PC9, PC10, PC11, PC12, PC13,
       PC14, PC15, PH, PL, RST, shift_register_1_p15, shift_register_1_p16, shift_register_1_p17,
       shift_register_1_p18, shift_register_1_p19, shift_register_1_p20, shift_register_1_p21,
       shift_register_1_p22, WE, X0, X1, X2, X3, X4, X5, X6, X7, XL, Y0, Y1, Y2, Y3, Y4, Y5, Y6, Y7, YL;
  wire [7:0] n74161_5_pin14, n74161_6_pin14;
  wire [15:0] n74157_2_pin9, rom_1_data;

  _74138 #(.ShowInternalStructure("true")) u_74138_1 (
    .pin1(IR5), .pin2(IR6), .pin3(IR7), .pin4(in_32), .pin5(in_32), .pin6(in_33), .pin7(n74138_1_pin7),
    .pin15(n74138_1_pin15), .pin14(n74138_1_pin14), .pin13(n74138_1_pin13), .pin12(n74138_1_pin12),
    .pin11(n74138_1_pin11), .pin10(n74138_1_pin10), .pin9(n74138_1_pin9));
  Clock clock_1 (.out(CLK1));
  not not_1 (RST, button_1_out);
  Button button_1 (.out(button_1_out));
  _74139 #(.ShowInternalStructure("true")) u_74139_1 (
    .pin1(in_27), .pin2(IR0), .pin3(IR1), .pin4(DE), .pin5(OE), .pin6(AE), .pin7(IE));  // open: pin15, pin14, pin13, pin12, pin11, pin10, pin9
  _74138 #(.ShowInternalStructure("true")) u_74138_2 (
    .pin1(IR2), .pin2(IR3), .pin3(IR4), .pin4(in_31), .pin5(in_31), .pin6(n74138_1_pin7),
    .pin7(n74138_2_pin7), .pin15(n74138_2_pin15), .pin14(n74138_2_pin14), .pin13(n74138_2_pin13),
    .pin12(n74138_2_pin12), .pin11(XL), .pin10(YL), .pin9(n74138_2_pin9));
  _74157 #(.ShowInternalStructure("true")) u_74157_1 (
    .pin1(EL), .pin2(X4), .pin3(D4), .pin4(n74157_2_pin9[4]), .pin5(X5), .pin6(D5), .pin7(n74157_2_pin9[5]),
    .pin15(in_37), .pin14(X6), .pin13(D6), .pin12(n74157_2_pin9[7]), .pin11(X7), .pin10(D7),
    .pin9(n74157_2_pin9[6]));
  _74157 #(.ShowInternalStructure("true")) u_74157_2 (
    .pin1(EL), .pin2(X1), .pin3(D1), .pin4(n74157_2_pin9[1]), .pin5(X2), .pin6(D2), .pin7(n74157_2_pin9[2]),
    .pin15(in_38), .pin14(X3), .pin13(D3), .pin12(n74157_2_pin9[3]), .pin11(X0), .pin10(D0),
    .pin9(n74157_2_pin9[0]));
  _74157 #(.ShowInternalStructure("true")) u_74157_3 (
    .pin1(EH), .pin2(Y5), .pin3(in_46), .pin4(n74157_2_pin9[13]), .pin5(Y6), .pin6(in_47),
    .pin7(n74157_2_pin9[14]), .pin14(Y3), .pin13(in_49), .pin12(n74157_2_pin9[11]), .pin11(Y1),
    .pin10(in_48), .pin9(n74157_2_pin9[9]));  // open: pin15
  _74157 #(.ShowInternalStructure("true")) u_74157_4 (
    .pin1(EH), .pin2(Y0), .pin3(in_51), .pin4(n74157_2_pin9[8]), .pin5(Y7), .pin6(in_52),
    .pin7(n74157_2_pin9[15]), .pin15(in_55), .pin14(Y2), .pin13(in_54), .pin12(n74157_2_pin9[10]),
    .pin11(Y4), .pin10(in_53), .pin9(n74157_2_pin9[12]));
  _7404 #(.ShowInternalStructure("true")) u_7404_1 (
    .pin13(CLK1), .pin12(n7404_1_pin12), .pin11(n7404_1_pin12), .pin10(CLK2));  // open: pin1, pin2, pin3, pin4, pin5, pin6, pin9, pin8
  _74161 #(.ShowInternalStructure("true")) u_74161_1 (
    .pin1(RST), .pin2(CLK1), .pin3(BUS0), .pin4(BUS1), .pin5(BUS2), .pin6(BUS3), .pin7(in_13),
    .pin15(n74161_1_pin15), .pin14(PC0), .pin13(PC1), .pin12(PC2), .pin11(PC3), .pin10(in_13), .pin9(PL));
  ROM #(.addrWidth(16), .dataWidth(16)) rom_1 (
    .addr({PC15, PC14, PC13, PC12, PC11, PC10, PC9, PC8, PC7, PC6, PC5, PC4, PC3, PC2, PC1, PC0}),
    .data(rom_1_data));
  or or_1 (WE, n74138_1_pin9, CLK1);
  or or_2 (or_2_out, n74138_1_pin10, n74138_1_pin7);
  or or_3 (or_3_out, n74138_1_pin13, n74138_1_pin12, n74138_1_pin10);
  or or_4 (or_4_out, n74138_1_pin15, n74138_1_pin13, n74138_1_pin12, n74138_1_pin11, n74138_1_pin7);
  or or_5 (or_5_out, n74138_1_pin15, n74138_1_pin14, n74138_1_pin13, n74138_1_pin11);
  or or_6 (or_6_out, n74138_1_pin7, IR7);
  _74240 #(.ShowInternalStructure("true")) u_74240_1 (
    .pin1(in_34), .pin2(or_2_out), .pin3(AR1), .pin4(or_4_out), .pin5(AR3), .pin6(or_6_out),
    .pin7(n74240_1_pin7), .pin9(n74240_1_pin9), .pin19(in_34), .pin18(AR0), .pin17(or_3_out), .pin16(AR2),
    .pin15(or_5_out), .pin14(AL), .pin12(n74240_1_pin12));  // open: pin8, pin13, pin11
  or or_7 (or_7_out, n74138_2_pin15, n74138_2_pin14, n74138_2_pin13, n74138_2_pin12);
  or or_8 (or_8_out, n74138_2_pin9, n74138_2_pin7);
  not not_2 (not_2_out, n74138_1_pin9);
  _74161 #(.ShowInternalStructure("true")) u_74161_2 (
    .pin1(RST), .pin2(CLK1), .pin3(BUS4), .pin4(BUS5), .pin5(BUS6), .pin6(BUS7), .pin7(in_14),
    .pin15(n74161_2_pin15), .pin14(PC4), .pin13(PC5), .pin12(PC6), .pin11(PC7), .pin10(n74161_1_pin15),
    .pin9(PL));
  // NoConnect on n74240_1_pin7
  _74139 #(.ShowInternalStructure("true")) u_74139_2 (
    .pin1(IR4), .pin2(IR3), .pin3(IR2), .pin4(n74139_2_pin4));  // open: pin5, pin6, pin7, pin15, pin14, pin13, pin12, pin11, pin10, pin9
  not not_3 (not_3_out, n74157_2_pin9[15]);
  not not_4 (not_4_out, WE);
  not not_5 (not_5_out, n74157_2_pin9[15]);
  not not_6 (not_6_out, OE);
  or or_9 (OL, or_8_out, not_2_out);
  or or_10 (LD, or_7_out, not_2_out);
  // NoConnect on n74240_1_pin12
  // NoConnect on n74240_1_pin9
  _74273 #(.ShowInternalStructure("true")) u_74273_1 (
    .pin1(in_15), .pin2(IR0), .pin3(rom_1_data[0]), .pin4(rom_1_data[1]), .pin5(IR1), .pin6(IR2),
    .pin7(rom_1_data[2]), .pin8(rom_1_data[3]), .pin9(IR3), .pin19(IR7), .pin18(rom_1_data[7]),
    .pin17(rom_1_data[6]), .pin16(IR6), .pin15(IR5), .pin14(rom_1_data[5]), .pin13(rom_1_data[4]),
    .pin12(IR4), .pin11(CLK1));
  _74273 #(.ShowInternalStructure("true")) u_74273_2 (
    .pin1(in_24), .pin2(D0), .pin3(rom_1_data[8]), .pin4(rom_1_data[9]), .pin5(D1), .pin6(D2),
    .pin7(rom_1_data[10]), .pin8(rom_1_data[11]), .pin9(D3), .pin19(D7), .pin18(rom_1_data[15]),
    .pin17(rom_1_data[14]), .pin16(D6), .pin15(D5), .pin14(rom_1_data[13]), .pin13(rom_1_data[12]),
    .pin12(D4), .pin11(CLK1));
  not not_7 (IX, n74138_2_pin7);
  or or_11 (EH, n74138_2_pin13, n74138_2_pin12, n74138_2_pin7);
  or or_12 (EL, n74138_2_pin14, n74138_2_pin12, n74138_2_pin7);
  RAM #(.addrWidth(15), .databus("bidir")) ram_1 (
    .addr(n74157_2_pin9[14:0]), .we(not_4_out), .oe(not_6_out), .clk(CLK2),
    .data({BUS7, BUS6, BUS5, BUS4, BUS3, BUS2, BUS1, BUS0}));
  or or_13 (PH, n74139_2_pin4, n74138_1_pin7);
  _74244 #(.ShowInternalStructure("true")) u_74244_1 (
    .pin1(DE), .pin2(D0), .pin3(BUS4), .pin4(D1), .pin5(BUS5), .pin6(D2), .pin7(BUS6), .pin8(D3),
    .pin9(BUS7), .pin19(DE), .pin18(BUS0), .pin17(D7), .pin16(BUS1), .pin15(D6), .pin14(BUS2), .pin13(D5),
    .pin12(BUS3), .pin11(D4));
  _74153 #(.ShowInternalStructure("true")) u_74153_1 (
    .pin1(n74138_1_pin7), .pin2(AC7), .pin3(in_29), .pin4(IR4), .pin5(IR3), .pin6(IR2), .pin7(n74153_1_pin7),
    .pin15(in_26), .pin14(CO), .pin13(in_26), .pin12(in_26), .pin11(in_26), .pin10(in_26));  // open: pin9
  and and_1 (PL, not_8_out, PH);
  _74161 #(.ShowInternalStructure("true")) u_74161_3 (
    .pin1(RST), .pin2(CLK1), .pin3(Y0), .pin4(Y1), .pin5(Y2), .pin6(Y3), .pin7(PL), .pin15(n74161_3_pin15),
    .pin14(PC8), .pin13(PC9), .pin12(PC10), .pin11(PC11), .pin10(n74161_2_pin15), .pin9(PH));
  not not_8 (not_8_out, n74153_1_pin7);
  // NoConnect on n74161_4_pin15
  _74161 #(.ShowInternalStructure("true")) u_74161_4 (
    .pin1(RST), .pin2(CLK1), .pin3(Y4), .pin4(Y5), .pin5(Y6), .pin6(Y7), .pin7(PL), .pin15(n74161_4_pin15),
    .pin14(PC12), .pin13(PC13), .pin12(PC14), .pin11(PC15), .pin10(n74161_3_pin15), .pin9(PH));
  // Shift_Register shift_register_1: pin names not known; wires that end beside it: in_39, in_41, OUT6, in_45, in_43, in_43, in_43, in_43, in_43, in_43, in_43, in_43, in_40, OUT5, shift_register_1_p15, shift_register_1_p16, shift_register_1_p17, shift_register_1_p18, shift_register_1_p19, shift_register_1_p20, shift_register_1_p21, shift_register_1_p22
  _74161 #(.ShowInternalStructure("true")) u_74161_5 (
    .pin1(OUT6), .pin2(CLK1), .pin7(in_35), .pin15(n74161_5_pin15), .pin14(n74161_5_pin14[0]),
    .pin13(n74161_5_pin14[1]), .pin12(n74161_5_pin14[2]), .pin11(n74161_5_pin14[3]), .pin10(in_35),
    .pin9(in_35));  // open: pin3, pin4, pin5, pin6
  _74161 #(.ShowInternalStructure("true")) u_74161_6 (
    .pin1(OUT7), .pin2(CLK1), .pin7(in_35), .pin15(n74161_6_pin15), .pin14(n74161_6_pin14[0]),
    .pin13(n74161_6_pin14[1]), .pin12(n74161_6_pin14[2]), .pin11(n74161_6_pin14[3]), .pin10(in_35),
    .pin9(in_35));  // open: pin3, pin4, pin5, pin6
  _74244 #(.ShowInternalStructure("true")) u_74244_2 (
    .pin1(IE), .pin2(shift_register_1_p15), .pin3(BUS4), .pin4(shift_register_1_p16), .pin5(BUS5),
    .pin6(shift_register_1_p17), .pin7(BUS6), .pin8(shift_register_1_p18), .pin9(BUS7), .pin19(IE),
    .pin18(BUS0), .pin17(shift_register_1_p19), .pin16(BUS1), .pin15(shift_register_1_p20), .pin14(BUS2),
    .pin13(shift_register_1_p21), .pin12(BUS3), .pin11(shift_register_1_p22));
  _74377 u_74377_1 (
    .pin1(LD), .pin2(AC3), .pin3(ALU3), .pin4(ALU2), .pin5(AC2), .pin6(AC1), .pin7(ALU1), .pin8(ALU0),
    .pin9(AC0), .pin19(AC6), .pin18(ALU7), .pin17(ALU6), .pin16(AC7), .pin15(AC4), .pin14(ALU4),
    .pin13(ALU5), .pin12(AC5), .pin11(CLK2));
  _74244 #(.ShowInternalStructure("true")) u_74244_3 (
    .pin1(AE), .pin2(AC0), .pin3(BUS7), .pin4(AC1), .pin5(BUS6), .pin6(AC2), .pin7(BUS5), .pin8(AC3),
    .pin9(BUS4), .pin19(AE), .pin18(BUS0), .pin17(AC7), .pin16(BUS1), .pin15(AC6), .pin14(BUS2), .pin13(AC5),
    .pin12(BUS3), .pin11(AC4));
  _74161 #(.ShowInternalStructure("true")) u_74161_7 (
    .pin1(OUT6), .pin2(CLK1), .pin7(in_36), .pin14(n74161_5_pin14[4]), .pin13(n74161_5_pin14[5]),
    .pin12(n74161_5_pin14[6]), .pin11(n74161_5_pin14[7]), .pin10(n74161_5_pin15), .pin9(in_36));  // open: pin3, pin4, pin5, pin6, pin15
  _74161 #(.ShowInternalStructure("true")) u_74161_8 (
    .pin1(OUT7), .pin2(CLK1), .pin7(in_36), .pin14(n74161_6_pin14[4]), .pin13(n74161_6_pin14[5]),
    .pin12(n74161_6_pin14[6]), .pin11(n74161_6_pin14[7]), .pin10(n74161_6_pin15), .pin9(in_36));  // open: pin3, pin4, pin5, pin6, pin15
  _74153 #(.ShowInternalStructure("true")) u_74153_2 (
    .pin1(in_9), .pin2(AC3), .pin3(AR3), .pin4(AR2), .pin5(AR1), .pin6(AR0), .pin7(n74153_2_pin7),
    .pin15(AL), .pin14(BUS3), .pin13(in_1), .pin12(in_5), .pin11(in_1), .pin10(in_5), .pin9(n74153_2_pin9));
  _74153 u_74153_3 (
    .pin1(AL), .pin2(BUS4), .pin3(in_16), .pin4(in_16), .pin5(in_20), .pin6(in_20), .pin7(n74153_3_pin7),
    .pin15(in_20), .pin14(AC4), .pin13(AR3), .pin12(AR2), .pin11(AR1), .pin10(AR0), .pin9(n74153_3_pin9));
  and and_2 (and_2_out, OUT6, OUT7);
  _74153 u_74153_4 (
    .pin1(in_10), .pin2(AC2), .pin3(AR3), .pin4(AR2), .pin5(AR1), .pin6(AR0), .pin7(n74153_4_pin7),
    .pin15(AL), .pin14(BUS2), .pin13(in_2), .pin12(in_6), .pin11(in_2), .pin10(in_6), .pin9(n74153_4_pin9));
  _74153 u_74153_5 (
    .pin1(AL), .pin2(BUS5), .pin3(in_17), .pin4(in_17), .pin5(in_21), .pin6(in_21), .pin7(n74153_5_pin7),
    .pin15(in_21), .pin14(AC5), .pin13(AR3), .pin12(AR2), .pin11(AR1), .pin10(AR0), .pin9(n74153_5_pin9));
  // RGB_Video rgb_video_1: pin names not known; wires that end beside it: RST, CLK1, and_2_out, n74161_5_pin14[6:0], n74161_6_pin14[6:0], {{8{OUT4}}, {8{OUT2}}, OUT1, OUT0, OUT1, OUT0, OUT1, OUT0, OUT1, OUT0}
  _74161 u_74161_9 (
    .pin1(in_25), .pin2(CLK2), .pin3(ALU4), .pin4(ALU5), .pin5(ALU6), .pin6(ALU7), .pin7(IX), .pin14(X4),
    .pin13(X5), .pin12(X6), .pin11(X7), .pin10(n74161_9_pin10), .pin9(XL));  // open: pin15
  _74161 u_74161_10 (
    .pin1(in_30), .pin2(CLK2), .pin3(ALU0), .pin4(ALU1), .pin5(ALU2), .pin6(ALU3), .pin7(IX),
    .pin15(n74161_9_pin10), .pin14(X0), .pin13(X1), .pin12(X2), .pin11(X3), .pin10(in_28), .pin9(XL));
  _74153 u_74153_6 (
    .pin1(in_11), .pin2(AC1), .pin3(AR3), .pin4(AR2), .pin5(AR1), .pin6(AR0), .pin7(n74153_6_pin7),
    .pin15(AL), .pin14(BUS1), .pin13(in_3), .pin12(in_7), .pin11(in_3), .pin10(in_7), .pin9(n74153_6_pin9));
  _74153 u_74153_7 (
    .pin1(AL), .pin2(BUS6), .pin3(in_18), .pin4(in_18), .pin5(in_22), .pin6(in_22), .pin7(n74153_7_pin7),
    .pin15(in_22), .pin14(AC6), .pin13(AR3), .pin12(AR2), .pin11(AR1), .pin10(AR0), .pin9(n74153_7_pin9));
  _74153 u_74153_8 (
    .pin1(in_12), .pin2(AC0), .pin3(AR3), .pin4(AR2), .pin5(AR1), .pin6(AR0), .pin7(n74153_8_pin7),
    .pin15(AL), .pin14(BUS0), .pin13(in_4), .pin12(in_8), .pin11(in_4), .pin10(in_8), .pin9(n74153_8_pin9));
  _74153 u_74153_9 (
    .pin1(AL), .pin2(BUS7), .pin3(in_19), .pin4(in_19), .pin5(in_23), .pin6(in_23), .pin7(n74153_9_pin7),
    .pin15(in_23), .pin14(AC7), .pin13(AR3), .pin12(AR2), .pin11(AR1), .pin10(AR0), .pin9(n74153_9_pin9));
  _74377 #(.ShowInternalStructure("true")) u_74377_2 (
    .pin1(YL), .pin2(Y0), .pin3(ALU0), .pin4(ALU1), .pin5(Y1), .pin6(Y2), .pin7(ALU2), .pin8(ALU3),
    .pin9(Y3), .pin19(Y7), .pin18(ALU4), .pin17(ALU5), .pin16(Y6), .pin15(Y5), .pin14(ALU6), .pin13(ALU7),
    .pin12(Y4), .pin11(CLK2));
  _74283 #(.ShowInternalStructure("true")) u_74283_1 (
    .pin1(ALU1), .pin2(n74153_6_pin9), .pin3(n74153_6_pin7), .pin4(ALU0), .pin5(n74153_8_pin7),
    .pin6(n74153_8_pin9), .pin7(AR0), .pin15(n74153_4_pin9), .pin14(n74153_4_pin7), .pin13(ALU2),
    .pin12(n74153_2_pin7), .pin11(n74153_2_pin9), .pin10(ALU3), .pin9(n74283_1_pin9));
  _74283 #(.ShowInternalStructure("true")) u_74283_2 (
    .pin1(ALU5), .pin2(n74153_5_pin7), .pin3(n74153_5_pin9), .pin4(ALU4), .pin5(n74153_3_pin7),
    .pin6(n74153_3_pin9), .pin7(n74283_1_pin9), .pin15(n74153_7_pin7), .pin14(n74153_7_pin9), .pin13(ALU6),
    .pin12(n74153_9_pin7), .pin11(n74153_9_pin9), .pin10(ALU7), .pin9(CO));
  _74377 #(.ShowInternalStructure("true")) u_74377_3 (
    .pin1(OL), .pin2(OUT3), .pin3(ALU3), .pin4(ALU2), .pin5(OUT2), .pin6(OUT1), .pin7(ALU1), .pin8(ALU0),
    .pin9(OUT0), .pin19(OUT7), .pin18(ALU7), .pin17(ALU6), .pin16(OUT6), .pin15(OUT5), .pin14(ALU5),
    .pin13(ALU4), .pin12(OUT4), .pin11(CLK2));

  // Other names for the same wires on the sheet: SER_DATA = in_45; SER_LATCH = in_44; SER_PULSE = in_42

  // Notes on the sheet:
  //   in_24: initial=0x1
  //   in_15: initial=0x1
  //   in_14: initial=0x1
  //   in_26: initial=0x1
  //   in_33: initial=0x1
  //   in_41: initial=0x1
  //   in_46: initial=0x1
  //   in_47: initial=0x1
  //   in_48: initial=0x1
  //   in_49: initial=0x1
  //   in_51: initial=0x1
  //   in_52: initial=0x1
  //   in_53: initial=0x1
  //   in_54: initial=0x1
  //   in_35: initial=0x1
  //   in_16: initial=0x1
  //   in_36: initial=0x1
  //   in_1: initial=0x1
  //   in_42: initial=0x1
  //   in_44: initial=0x1
  //   in_45: initial=0x1
  //   in_17: initial=0x1
  //   in_2: initial=0x1
  //   in_25: initial=0x1
  //   in_30: initial=0x1
  //   in_28: initial=0x1
  //   in_18: initial=0x1
  //   in_3: initial=0x1
  //   in_19: initial=0x1
  //   in_4: initial=0x1
  //   in_13: initial=0x1
  //   RAM
  //   命令デコーダ
  //   BUS_ACCESS_DECODER
  //   MODE_DECODER
  //   INSTRUCTION_DECODER
  //   クロック回路
  //   リセット回路
  //   ROM
  //   プログラムカウンタ
  //   contents of rom_1 (hex, n*v repeats v):
  //   0 1880 18c0 c17f c17c 1 d601 ff 6900 ca00 c200 6900 ec0c ff 6900 ca00 6100 f015 101 fc06 8200 ff
  //   c200 ec17 a001 100 ec16 a001 1 1880 18c0 0 d218 d619 106 f426 8d00 60bf c206 107 f42b 8106 60c1 c207
  //   8108 c208 118 8001 ec22 d218 119 8001 ec22 d619 3 1880 18c0 ee c216 9002 1 d617 dc59 dc5f dc2b dc22
  //   dcb4 dce2 dc00 dc00 dcfc dc00 2 c205 ff c20e c20f c210 c211 c212 7 1880 18c0 0 c200 c202 c22c f 1880
  //   18c0 c213 c214 1401 e003 c22e 48 c221 0 c21c 1401 caf9 caf6 caf7 c22c c21a 2 c21b f6 c20a c20b c20c
  //   ad c222 bd c224 f3 c225 116 a002 c216 c17f c17c 11d 1403 e0cb e8 200 200 1403 e0cb f6 1403 e0cb f6
  //   1403 e0cb f6 1403 e0cb f6 1403 e0cb f6 1403 e0cb f6 1403 e0cb f6 1403 e0cb f6 1403 e0cb f6 1403 e0cb
  //   f6 1414 e05c 12a 1414 e094 128 1403 e0cb f6 1403 e0cb f6 1403 e0cb f6 1412 e042 0 1403 e0cb f6 1403
  //   e0cb f6 1403 e0cb f6 1403 e0cb f6 1403 e0cb f6 1403 e0cb f6 1403 e0cb f6 1403 e0cb f6 1403 e0cb f6
  //   1403 e0cb f6 1403 e0cb f6 1403 e0cb f6 1403 e0cb f6 1403 e0cb f6 1403 e0cb f6 1403 e0cb f6 1403 e0cb
  //   f6 1414 e027 119 1414 e000 1525 1413 e000 118 1413 e078 119 14f7 e06c 119 200 200 1924 200 1403 e0cb
  //   f5 c318 0 c219 200 1403 e0cb f4 1505 e0ff 7f c0 c21f 80 c220 b3 c209 1 c280 810e c20e 6107 610f 8106
  //   c206 8108 c208 e816 fc17 6053 606c 8107 c207 12d f01d fc1e a001 12f c22d f022 fc23 0 1 812e ec27
  //   fc28 e8 e42c c22e 8048 fe00 fc48 f c22e fc48 2114 f 7 3 1 2 4 8 4 2 1 3 7 f e c 8 4 2 1 2 4 8 c e
  //   c214 10 c20d 10e f052 55 c21e 1505 e0ff 23 1412 e000 1401 121 20fb c221 12c ec5c fc5d 0 f0 4114 c214
  //   12c f063 fc64 a001 0 c22c 191f 102 2121 8001 1920 d602 7f 29fe 89fc cafe 3080 500 89ff 89fd caff
  //   20fc 69fb 1200 9fa 1407 8d00 e87d fc7e 203f 3f 8103 c203 113 1412 191f 109 f4b1 8002 c209 a0bd ec8d
  //   a10d 40 fc92 c21f ec91 c0 fc93 c21f 11f 200 6040 c220 109 60cf ec9a fc9b c30f c000 109 2006 f0a6 103
  //   a4 c21e 1505 e0ff 35 fc66 191f 400f 2114 c213 c003 af c21e 1505 e0ff 33 fc66 191f e025 1401 111 60ef
  //   ecbe 112 a001 c212 207f f0c6 ee fcc5 fcc4 1 ecbf a001 200 80 c212 fccb 200 c216 1 c217 2 c205 111
  //   60df ece2 10b e8d5 10a c20b 10c c20a fcda f6 a c20b c20a 200 c20c 35 ecdc a001 200 c211 fcea 0 102
  //   2003 c202 ea c21e 1505 e0ff 26 1401 9f9 c209 c21f ecf1 fcf2 1 ec c20d 102 2121 8001 1402 e0b1 1880
  //   6*200 fcae 102 ca c20d 1401 1109 d00 de00 c220 d00 911f 1520 c0 160*5d00 18c0 102 2121 8001 1880
  //   d602 7f 29fe 89fc cafe 3080 500 89ff 89fd caff 20fc 69fb 1200 9fa 1407 8d00 e8c4 fcc5 203f 3f 8103
  //   c203 113 fd0d 18c0 d3 c20d 1401 109 9001 11f 8d00 fd0a d21f dc c20d 103 400f 2114 c213 c003 fd0b
  //   111f 111f 109 a0ee f0e5 80f0 c209 1 fd0c c20d c003 e9 fd0c c20d 1401 e004 c0 120 8080 d220 11f a500
  //   f0f4 c21f fcf6 1 c20d ff c21e 1505 e0ff 3c 4*200 fc03 1517 8115 e80b c215 116 8002 d216 d00 de00
  //   fe00 d00 800e e40c a001 1401 e11e 0 c218 de00 d00 c219 116 8001 c216 f6 fc01 1200 500 1404 e013 c218
  //   140b e0d2 1200 8001 c21d 500 c218 111d 500 c219 fc01 f6 1200 8001 c21d 118 c600 111d 119 c600 fc01
  //   f6 119 ec40 c21d 118 f043 1 c21d d00 fe00 11d ec45 f048 d00 200 fc3d d00 116 fc4a 8001 de00 d00 c216
  //   fc01 f2 f845 e448 d00 f445 e848 d00 e845 f448 d00 e445 f848 d00 c218 0 c219 fc00 f8 1200 118 c600
  //   fc00 f8 111c 500 c21a 11c 9001 500 c21b 11c 8002 c21c 116 a001 c216 fc00 f3 f045 ec48 d00 11c b001
  //   11b c600 11c a002 d21c 11a fc6d c600 1519 e0fb 8118 1404 e011 2118 140b e0c6 116 4118 c218 fc01 f9
  //   6118 c218 fc01 f9 c216 fc00 f9 1200 1404 e0e4 1 140b e0de 1200 8001 c21d 118 8500 c218 e8a3 a500
  //   fca5 4500 2500 200 3080 500 8119 111d 8500 c219 fc01 f2 1404 e062 116 a002 c216 fccb f6 8115 e8af
  //   1523 e122 1200 8001 c21d 118 e8c1 a500 c218 fcc4 4500 c218 2500 200 3080 119 a500 111d a500 c219 f2
  //   fc01 1517 1404 e007 c21d 116 8002 c21a 117 c21b 111d 500 a002 c216 11d 9001 500 d617 fc01 f3 811c
  //   c21c fc01 f9 1404 e018 c21d 1404 e026 c21d 1404 e035 118 1404 e041 1404 e04c 1404 e057 c21d 1404
  //   e06d c21d 1404 e07a 1404 e086 1404 e091 1404 e09c c21d 11a a002 c216 11b c217 1403 e0cb f6 116 8002
  //   c218 117 c219 11d c216 1403 e000 f4 200 c218 0 c219 1403 e0cb f5 8118 c218 e81e a11d fc20 411d 211d
  //   200 3080 500 8119 1403 e0ca c21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
  //   5
  //   7
  //   2
  //   3
  //   5
  //   AR0
  //   AR1
  //   AR2
  //   AR3
  //   AR3
  //   0
  //   1
  //   2
  //   3
  //   6
  //   7
  //   To RAM
  //   6
  //   7
  //   2
  //   3
  //   7
  //   1
  //   3
  //   7
  //   InstructionRegister
  //   DataRegister
  //   IR2
  //   IR3
  //   IR4
  //   5
  //   4
  //   To ALU
  //   To User Registers
  //   To memory address unit
  //   To user registeres
  //   To program counter
  //   I/O
  //   ALU
  //   Register
  //   Bus gateway AC
  //   Accumlator
  //   X register
  //   Y register
  //   Output register
endmodule
